# Fritzing sketch 02-potentiometer (saved by Fritzing 0.8.7b)
breadboards: 1

parts:
  MVPROG1 = MicroView with Programmer [part_number=MicroView package="16pin wide"]
  R1 = TRIMPOT [package=3386u]

nets:
  N1: MVPROG1.A1, R1.WIPER
  N2: MVPROG1.GND, R1.CCW
  N3: MVPROG1.5V, R1.CW

custom parts:
  MicroView with Programmer: MicroView - Chip-sized Arduino with OLED display.
