# Fritzing sketch 03-rgb-led (saved by Fritzing 0.8.7b)
breadboards: 1

parts:
  MVPROG1 = MicroView with Programmer [part_number=MicroView package="16pin wide"]
  LED1 = RGB LED (com. cathode, rbg) [package="5 mm [THT]"]
  R1 = Resistor [tolerance=±5% resistance=330 package=THT]
  R2 = Resistor [tolerance=±5% resistance=330 package=THT]
  R3 = Resistor [tolerance=±5% resistance=330 package=THT]

nets:
  N1: MVPROG1.GND, LED1.common_cathode
  N2: MVPROG1.D3, R3.Pin_0
  N3: MVPROG1.D5, R2.Pin_0
  N4: MVPROG1.D6, R1.Pin_0
  N5: LED1.red_anode, R1.Pin_1
  N6: LED1.blue_anode, R2.Pin_1
  N7: LED1.green_anode, R3.Pin_1

custom parts:
  MicroView with Programmer: MicroView - Chip-sized Arduino with OLED display.
