# Fritzing sketch 04-push-buttons (saved by Fritzing 0.8.7b)
breadboards: 1

parts:
  MVPROG1 = MicroView with Programmer [part_number=MicroView package="16pin wide"]
  S2 = Button for MicroView [package=tactile-pth]

nets:
  N1: MVPROG1.A0, S2.2
  N2: MVPROG1.GND, S2.1

custom parts:
  MicroView with Programmer: MicroView - Chip-sized Arduino with OLED display.
  Button for MicroView: SIK 12mm Buttom
