# Fritzing sketch 05-photo-resistor (saved by Fritzing 0.8.7b)
breadboards: 1

parts:
  MVPROG1 = MicroView with Programmer [part_number=MicroView package="16pin wide"]
  R2 = Photocell (LDR) [package=THT]
  R3 = Resistor [tolerance=±5% resistance=10k package=THT]

nets:
  N1: MVPROG1.A0, R2.pin_1, R3.Pin_0
  N2: MVPROG1.GND, R2.pin_0
  N3: MVPROG1.5V, R3.Pin_1

custom parts:
  MicroView with Programmer: MicroView - Chip-sized Arduino with OLED display.
