# Fritzing sketch 06-temperature-sensor (saved by Fritzing 0.8.7b)
breadboards: 1

parts:
  MVPROG2 = MicroView with Programmer [part_number=MicroView package="16pin wide"]
  U1 = TMP36 [package=to-92-kit]

nets:
  N1: MVPROG2.A0, U1.VOUT
  GND: MVPROG2.GND, U1.GND
  5V: MVPROG2.5V, U1.VCC

custom parts:
  MicroView with Programmer: MicroView - Chip-sized Arduino with OLED display.
