# Fritzing sketch 09-motors (saved by Fritzing 0.8.7b)
breadboards: 1

parts:
  MVPROG1 = MicroView with Programmer [part_number=MicroView package="16pin wide"]
  R1 = Resistor [tolerance=±5% resistance=330 package=THT]
  M1 = DC Motor
  Q1 = TRANSISTOR_NPN [package=to-92]
  D1 = Diode for MicroView [package=diode-1n4148]

nets:
  N1: MVPROG1.GND, Q1.C
  N2: MVPROG1.D2, R1.Pin_0
  N3: MVPROG1.5V, M1.pin_1, D1.C
  N4: R1.Pin_1, Q1.B
  N5: M1.pin_2, Q1.E, D1.A

custom parts:
  MicroView with Programmer: MicroView - Chip-sized Arduino with OLED display.
  Diode for MicroView: Diode These are standard reverse protection diodes and small signal diodes. SMA package can handle up to about 1A. SOD-323 can handle about 200mA. What the SOD-323 package when ordering, there are some mfgs out there that are 5-pin packages.
