# Fritzing sketch 10-relay (saved by Fritzing 0.8.7b)
breadboards: 1

parts:
  MVPROG2 = MicroView with Programmer [part_number=MicroView package="16pin wide"]
  R1 = Resistor [tolerance=±5% resistance=330 package=THT]
  Q1 = NPN-Transistor [package="SOT-23 [SMD]"]
  U1 = Relay for MicroView [package=relay-g5q]
  R2 = Resistor [tolerance=±5% resistance=220 package=THT]
  LED2 = LED - 5mm [color="Yellow (595nm)" package="5 mm [THT]"]
  LED1 = LED - 5mm [color="Red (633nm)" package="5 mm [THT]"]
  D1 = Diode for MicroView [package=diode-1n4148]

nets:
  N1: MVPROG2.GND, Q1.1, LED2.cathode, LED1.cathode
  N2: MVPROG2.D2, R1.Pin_1
  N3: MVPROG2.5V, U1.COIL2, R2.Pin_0, D1.C
  N4: R1.Pin_0, Q1.0
  N5: Q1.2, U1.COIL1, D1.A
  N6: U1.MAIN, R2.Pin_1
  N7: U1.NO, LED2.anode
  N8: U1.NC, LED1.anode

custom parts:
  MicroView with Programmer: MicroView - Chip-sized Arduino with OLED display.
  Relay for MicroView: SPDT relay (COM-00101)
  Diode for MicroView: Diode These are standard reverse protection diodes and small signal diodes. SMA package can handle up to about 1A. SOD-323 can handle about 200mA. What the SOD-323 package when ordering, there are some mfgs out there that are 5-pin packages.
