# Fritzing sketch 11-soft-pot (saved by Fritzing 0.8.7b)
breadboards: 1

parts:
  MVPROG2 = MicroView with Programmer [part_number=MicroView package="16pin wide"]
  R1 = Resistor [tolerance=±5% resistance=330 package=THT]
  R2 = Resistor [tolerance=±5% resistance=330 package=THT]
  Q1 = NPN-Transistor [package="TO92 [THT]"]  # not connected

nets:
  N1: MVPROG2.A0, R1.Pin_0
  N2: MVPROG2.5V, R2.Pin_0

custom parts:
  MicroView with Programmer: MicroView - Chip-sized Arduino with OLED display.
  NPN-Transistor: A standard NPN-transistor
